# Fritzing sketch b3it-p1 (saved by Fritzing 0.9.4)
breadboards: 1

parts:
  Part2 = Arduino Uno (Rev3)
  HC-SR04_Sensor_1 = HC-SR04 Ultrasonic Distance Sensor
  Motion_sensor = HC-SR501 Body Sensor Module
  R1 = Photocell (LDR) [package=THT]
  R2 = Resistor [tolerance=±5% resistance=10k package="0603 [SMD]"]
  DS1 = DS18B20 1-Wire Temperature Sensor [part_number=DS18B20]
  R3 = Resistor [tolerance=±5% resistance=2.2k package="0603 [SMD]"]
  Magnetic_sensor = Pushbutton [package=THT]
  R4 = Resistor [tolerance=±5% resistance=10k package="0603 [SMD]"]
  LCD1 = LCD screen
  U1 = POT [package=3362u]
  R5 = Resistor [tolerance=±5% resistance=220 package="0603 [SMD]"]
  Q1 = Basic FET N-Channel [package="TO220 [THT]"]
  U3 = Mystery Part - 10 pins [chip_label="Missing Piece" package=THT]
  R6 = Resistor [tolerance=±5% resistance=10k package="0603 [SMD]"]
  LED1 = smd LED [color="Red (633nm)" package="1206 [SMD]"]
  LED2 = smd LED [color="Green (555nm)" package="1206 [SMD]"]
  R7 = Resistor [tolerance=±5% resistance=220 package="0603 [SMD]"]
  R8 = Resistor [tolerance=±5% resistance=220 package="0603 [SMD]"]
  S1 = Pushbutton [package="[THT]"]
  S2 = Pushbutton [package="[THT]"]
  S3 = Pushbutton [package="[THT]"]
  R11 = Resistor [tolerance=±5% resistance=10k package="0603 [SMD]"]
  R12 = Resistor [tolerance=±5% resistance=10k package="0603 [SMD]"]
  R13 = Resistor [tolerance=±5% resistance=10k package="0603 [SMD]"]

nets:
  N1: Part2.A0, Motion_sensor.OUT
  N2: Part2.A1, R1.pin_1, R2.Pin_1
  N3: Part2.A2, DS1.DQ, R3.Pin_0
  N4: Part2.A3, Magnetic_sensor.leg1, R4.Pin_0
  N5: Part2.A4/SDA, S1.Pin_1, S1.Pin_2, R11.Pin_0
  N6: Part2.D8, LCD1.DB7
  N7: Part2.D9_PWM, LCD1.DB6
  N8: Part2.D10_PWM/SS, LCD1.DB5
  N9: Part2.D11_PWM/MOSI, LCD1.DB4
  N10: Part2.D12/MISO, Q1.gate, R6.Pin_0
  N11: Part2.D13/SCK, LED1.anode, LED2.cathode
  N12: Part2.D2, S2.Pin_3, S2.Pin_4, R12.Pin_0
  N13: Part2.D3_PWM, S3.Pin_3, S3.Pin_4, R13.Pin_0
  N14: Part2.D4, HC-SR04_Sensor_1.TRIG
  N15: Part2.D5_PWM, HC-SR04_Sensor_1.ECHO
  N16: Part2.D6_PWM, LCD1.E
  N17: Part2.D7, LCD1.RS
  VCC: Part2.5V, HC-SR04_Sensor_1.VCC, Motion_sensor.VCC, R1.pin_0, DS1.VDD, R3.Pin_1, R4.Pin_1, R7.Pin_1, R11.Pin_1, R12.Pin_1, R13.Pin_1
  GND: Part2.GND, HC-SR04_Sensor_1.GND, Motion_sensor.GND, R2.Pin_0, DS1.GND, Magnetic_sensor.leg0, LCD1.VSS, U1.E, Q1.source, U3.pin10, R6.Pin_1, R8.Pin_0, S1.Pin_3, S1.Pin_4, S2.Pin_1, S2.Pin_2, S3.Pin_1, S3.Pin_2
  N18: LCD1.VDD, U1.A
  N19: LCD1.V0, U1.S
  N20: LCD1.LED+, R5.Pin_1
  N21: Q1.drain, U3.pin1
  N22: LED1.cathode, LED2.anode, R7.Pin_0, R8.Pin_1

custom parts:
  HC-SR501 Body Sensor Module: Pyroelectric Infrared PIR Motion Sensor Detector Module
  Mystery Part - 10 pins: A dummy, proxy, ersatz, stand-in part for whatever you want. With 10 pins on a 100 mil inline pin header footprint.
